// Logisim project d8421.circ as structural Verilog: 5 circuits, main circuit main
module main (
  input  [3:0] in_1,
  output [3:0] out_2
);

  Hex_Digit_Display hex_digit_display_1 (.value(out_2));  // open: dp
  Hex_Digit_Display hex_digit_display_2 (.value(in_1));  // open: dp
  Y1 Y1 (.X1(in_1[3]), .X2(in_1[2]), .X3(in_1[1]), .X4(in_1[0]), .Y1(out_2[3]));
  Y2 Y2 (.X1(in_1[3]), .X2(in_1[2]), .X3(in_1[1]), .X4(in_1[0]), .out_5(out_2[2]));
  Y4 Y4 (.X1(in_1[3]), .X2(in_1[2]), .X3(in_1[1]), .X4(in_1[0]), .out_5(out_2[0]));
  Y3 Y3 (.X1(in_1[3]), .X2(in_1[2]), .X3(in_1[1]), .X4(in_1[0]), .out_5(out_2[1]));
endmodule

module Y1 (
  input  X1,
  input  X2,
  input  X3,
  input  X4,
  output Y1
);

  wire and_1_out, and_2_out, not_1_out, not_2_out, not_3_out;

  not not_1 (not_1_out, X2);
  not not_2 (not_2_out, X3);
  not not_3 (not_3_out, X1);
  and and_1 (and_1_out, X1, not_1_out, not_2_out);
  or or_1 (Y1, and_1_out, and_2_out);
  and and_2 (and_2_out, not_3_out, X2, X3, X4);
endmodule

module Y2 (
  input  X1,
  input  X2,
  input  X3,
  input  X4,
  output out_5
);

  wire and_1_out, and_2_out, and_3_out, not_1_out, not_2_out, not_3_out, not_4_out, not_5_out, not_6_out;

  or or_1 (out_5, and_1_out, and_2_out, and_3_out);
  and and_1 (and_1_out, not_1_out, X2, not_2_out);
  and and_2 (and_2_out, not_3_out, X2, not_4_out);
  not not_1 (not_1_out, X1);
  not not_2 (not_2_out, X4);
  not not_3 (not_3_out, X1);
  not not_4 (not_4_out, X3);
  and and_3 (and_3_out, not_5_out, not_6_out, X3, X4);
  not not_5 (not_5_out, X1);
  not not_6 (not_6_out, X2);
endmodule

module Y3 (
  input  X1,
  input  X2,
  input  X3,
  input  X4,
  output out_5
);

  wire and_1_out, and_2_out, and_3_out, not_1_out, not_2_out, not_3_out, not_4_out, not_5_out, not_6_out;

  or or_1 (out_5, and_1_out, and_2_out, and_3_out);
  and and_1 (and_1_out, not_2_out, not_1_out, X4);
  and and_2 (and_2_out, not_3_out, X3, not_4_out);
  not not_1 (not_1_out, X3);
  not not_2 (not_2_out, X1);
  not not_3 (not_3_out, X1);
  not not_4 (not_4_out, X4);
  and and_3 (and_3_out, not_6_out, not_5_out, X4);
  not not_5 (not_5_out, X3);
  not not_6 (not_6_out, X2);
endmodule

module Y4 (
  input  X1,
  input  X2,
  input  X3,
  input  X4,
  output out_5
);

  wire and_1_out, and_2_out, not_1_out, not_2_out, not_3_out, not_4_out, not_5_out;

  or or_1 (out_5, and_2_out, and_1_out);
  and and_1 (and_1_out, not_2_out, not_5_out);
  and and_2 (and_2_out, not_1_out, not_4_out, not_3_out);
  not not_1 (not_1_out, X2);
  not not_2 (not_2_out, X1);
  not not_3 (not_3_out, X4);
  not not_4 (not_4_out, X3);
  not not_5 (not_5_out, X4);
endmodule
