// Logisim project summator2.circ as structural Verilog: 2 circuits, main circuit main
// A
module main (
  input  [7:0] A,
  input  [7:0] B,
  output [7:0] A_2
);

  wire sn_1_tran_2, sn_2_tran_2, sn_3_tran_2, sn_4_tran_2, sn_5_tran_2, sn_6_tran_2, sn_7_tran_2;

  sn sn_1 (.A(A[0]), .B(B[0]), .Tran(1'b0), .Res(A_2[0]), .Tran_2(sn_1_tran_2));
  sn sn_2 (.A(A[1]), .B(B[1]), .Tran(sn_1_tran_2), .Res(A_2[1]), .Tran_2(sn_2_tran_2));
  sn sn_3 (.A(A[2]), .B(B[2]), .Tran(sn_2_tran_2), .Res(A_2[2]), .Tran_2(sn_3_tran_2));
  sn sn_4 (.A(A[3]), .B(B[3]), .Tran(sn_3_tran_2), .Res(A_2[3]), .Tran_2(sn_4_tran_2));
  sn sn_5 (.A(A[5]), .B(B[5]), .Tran(sn_6_tran_2), .Res(A_2[5]), .Tran_2(sn_5_tran_2));
  sn sn_6 (.A(A[4]), .B(B[4]), .Tran(sn_4_tran_2), .Res(A_2[4]), .Tran_2(sn_6_tran_2));
  sn sn_7 (.A(A[6]), .B(B[6]), .Tran(sn_5_tran_2), .Res(A_2[6]), .Tran_2(sn_7_tran_2));
  sn sn_8 (.A(A[7]), .B(B[7]), .Tran(sn_7_tran_2), .Res(A_2[7]));  // open: Tran_2
endmodule

module sn (
  input  A,
  input  B,
  input  Tran,
  output Res,
  output Tran_2
);

  wire and_1_out, and_2_out, xor_1_out;

  xor xor_1 (xor_1_out, A, B);
  xor xor_2 (Res, xor_1_out, Tran);
  and and_1 (and_1_out, xor_1_out, Tran);
  and and_2 (and_2_out, B, A);
  or or_1 (Tran_2, and_1_out, and_2_out);
endmodule
